# Fritzing sketch _Schaltplan (saved by Fritzing 0.9.3b)
breadboards: 1

parts:
  ZS-042_RTC1 = ZS-042 RTC Module  # not connected
  R1 = Photocell (LDR) [package=THT]
  IR2 = TSOP312.., 314.. [part_number="IR Receiver TSOP31240" package=THT]
  J3 = female pin header, 4 pins [form="♀ (female)" part_number="DCF77 Header 3V3, GND, DATA, PON"]
  J4 = female pin header, 2 pins [form="♀ (female)" part_number="5 Volt in"]
  R9 = Resistor [tolerance=±5% resistance=10k package=THT]
  J5 = Piezo Speaker
  WeMos_D1_Mini2 = WeMos D1 Mini  # not connected

nets:
  N1: R1.pin_0, R9.Pin_1
  N2: R1.pin_1, IR2.GND, J3.pin3, J4.pin2, J5.pin1
  N3: IR2.Vs, R9.Pin_0
  N4: J3.pin4, J4.pin1

notes:
  5Vin
  3V3
  LED-Stripe Header:
  5V, GND, (CLOCK), DATA
